# Fritzing sketch esp32-computer-mockup-1 (saved by Fritzing 0.9.4)
breadboards: 4

parts:
  U6 = ESP32S-HiLetgo [part_number=ESP32S-HiLetgo]
  U1 = ESP32S-HiLetgo [part_number=ESP32S-HiLetgo]
  U4 = ESP32S-HiLetgo [part_number=ESP32S-HiLetgo]
  U5 = ESP32S-HiLetgo [part_number=ESP32S-HiLetgo]
  U7 = ESP32S-HiLetgo [part_number=ESP32S-HiLetgo]
  U3 = ESP32S-HiLetgo [part_number=ESP32S-HiLetgo]
  S1 = Pushbutton [package="[SMD]"]

nets:
  N1: U6.GPIO14, U1.GPIO14, U4.GPIO14, U5.GPIO14, U7.GPIO14, U3.GPIO14
  N2: U6.GPIO12, U1.GPIO12, U4.GPIO12, U5.GPIO12, U7.GPIO12, U3.GPIO12
  GND: U6.GND, U1.GND, U4.GND, U5.GND, U7.GND, U3.GND
  N3: U6.GPIO11, U1.GPIO11, U4.GPIO11, U5.GPIO11, U7.GPIO11, U3.GPIO11, S1.Pin_1, S1.Pin_2
  VIN: U6.VIN, U1.VIN, U4.VIN, U5.VIN, U7.3.3, U7.VIN, U3.VIN, S1.Pin_3, S1.Pin_4

notes:
  orange=mosi;green=miso;cyan=clk;blue=data;

custom parts:
  ESP32S-HiLetgo: HiLetgo ESP-WROOM-32 ESP32 ESP-32S Development Board 2.4GHz Dual-Mode WiFi + Bluetooth Dual Cores Microcontroller The ESP32 integrated with Antenna switches, RF Balun, power amplifiers, low-noise amplifiers, filters, and management modules, and the entire solution occupies the least area of PCB. 2.4 GHz Wi-Fi plus Bluetooth dual-mode chip, with TSMC Ultra-low power consumption 40nm technology,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
